// Logisim project labo_alu_etu.circ as structural Verilog: 6 circuits, main circuit ALU_MAXV
module ALU_MAXV (
  input  [3:0] a_i,
  input  [3:0] b_i,
  output [3:0] c_o,
  output erreur_o
);

  wire [5:0] opcode_i_sw6;

  DipSwitch opcode_i (
    .sw1(opcode_i_sw6[5]), .sw2(opcode_i_sw6[4]), .sw3(opcode_i_sw6[3]), .sw4(opcode_i_sw6[2]),
    .sw5(opcode_i_sw6[1]), .sw6(opcode_i_sw6[0]));  // open: sw7, sw8
  ALU_Top alu_inst (.a_i(a_i), .b_i(b_i), .op_i(opcode_i_sw6), .c_o(c_o), .erreur_o(erreur_o));

  // Notes on the sheet:
  //   Attention, votre version de Logisim
  //   ne contient pas de tracker. Si vous
  //   enregistrez votre projet, toutes les
  //   informations du tracker seront
  //   définitivement effacées.
endmodule

module ALU_Top (
  input  [3:0] a_i,
  input  [3:0] b_i,
  input  [5:0] op_i,
  output [3:0] c_o,
  output erreur_o
);


  // Notes on the sheet:
  //   Attention, votre version de Logisim
  //   ne contient pas de tracker. Si vous
  //   enregistrez votre projet, toutes les
  //   informations du tracker seront
  //   définitivement effacées.
endmodule

module Add_Sub4Bits (
  input  [3:0] a_i,
  input  [3:0] b_i,
  input  [1:0] op_i,
  output [3:0] r_o,
  output overflow_o,
  output carry_o,
  output Negative_o,
  output zero_o
);


  // Notes on the sheet:
  //   Attention, votre version de Logisim
  //   ne contient pas de tracker. Si vous
  //   enregistrez votre projet, toutes les
  //   informations du tracker seront
  //   définitivement effacées.
endmodule

module Comparateur (
  input  carry_i,
  input  Negative_i,
  input  zero_i,
  input  a_i,
  input  b_i,
  input  [2:0] op_i,
  output [3:0] cmp_o
);


  // Notes on the sheet:
  //   Attention, votre version de Logisim
  //   ne contient pas de tracker. Si vous
  //   enregistrez votre projet, toutes les
  //   informations du tracker seront
  //   définitivement effacées.
endmodule

module UniteLogique (
  input  [3:0] a_i,
  input  [3:0] b_i,
  input  [1:0] op_i,
  output [3:0] f_o
);


  // Notes on the sheet:
  //   Attention, votre version de Logisim
  //   ne contient pas de tracker. Si vous
  //   enregistrez votre projet, toutes les
  //   informations du tracker seront
  //   définitivement effacées.
endmodule

module Custom (
  input  [3:0] a_i,
  output [3:0] s_o
);


  // Notes on the sheet:
  //   Attention, votre version de Logisim
  //   ne contient pas de tracker. Si vous
  //   enregistrez votre projet, toutes les
  //   informations du tracker seront
  //   définitivement effacées.
endmodule
